// Logisim project CU.circ as structural Verilog: 1 circuit, main circuit main
module main (
  input  MOV,
  input  MOI,
  input  LOAD,
  input  STORE,
  input  ADD,
  input  ADI,
  input  SUB,
  input  SUI,
  input  AND,
  input  ANI,
  input  OR,
  input  ORI,
  input  HLT,
  input  CLK,
  output STAGE_1,
  output STAGE_2,
  output STAGE_3,
  output STAGE_4,
  output STAGE_5
);

  wire ENABLE_ALU, ENABLE_MUX_B, ENABLE_MUX_Y, ENABLE_RA, ENABLE_RB, ENABLE_SELECT_RY, or_1_out, or_2_out,
       or_3_out, or_4_out, or_5_out, or_6_out, or_7_out, SELECT_MUX_MEM, SELECT_MUX_Y, WRITE_MEM;
  wire [2:0] counter_1_q;

  or or_1 (or_1_out, MOV, MOI, LOAD, STORE, ADD, ADI, SUB, SUI, AND, ANI, OR, ORI);
  or or_2 (or_2_out, MOI, LOAD, STORE, ADI, SUI, ANI, ORI);
  and and_1 (ENABLE_ALU, STAGE_3, or_1_out);
  and and_2 (ENABLE_MUX_B, STAGE_3, or_2_out);
  Counter #(.width(3), .max('h4)) counter_1 (.D(3'b000), .Q(counter_1_q), .clk(CLK));  // open: load, count, carry, clr
  Decoder #(.select(3), .enable("false")) decoder_1 (
    .out0(STAGE_1), .out1(STAGE_2), .out2(STAGE_3), .out3(STAGE_4), .out4(STAGE_5), .sel(counter_1_q));  // open: out5, out6, out7
  or or_3 (or_3_out, STORE, ADD, SUB, AND, OR);
  or or_4 (or_4_out, MOV, MOI, LOAD, STORE, ADD, ADI, SUB, SUI, AND, ANI, OR, ORI);
  or or_5 (or_5_out, STORE, LOAD);
  or or_6 (or_6_out, or_3_out, MOV, LOAD, ADI, SUI, ANI, ORI);
  and and_3 (ENABLE_RB, STAGE_2, or_3_out);
  and and_4 (ENABLE_MUX_Y, STAGE_1, or_4_out);
  and and_5 (SELECT_MUX_MEM, STAGE_4, or_5_out);
  and and_6 (SELECT_MUX_Y, STAGE_4, LOAD);
  and and_7 (WRITE_MEM, STAGE_4, STORE);
  and and_8 (ENABLE_RA, or_6_out, STAGE_2);
  or or_7 (or_7_out, MOV, MOI, LOAD, STORE, ADD, ADI, SUB, SUI, AND, ANI, OR, ORI);
  and and_9 (ENABLE_SELECT_RY, STAGE_5, or_7_out);

  // Other names for the same wires on the sheet: ENABLE_RY = ENABLE_MUX_Y; ENABLE_RZ = ENABLE_ALU;
  //   ENABLE_SELECT_RA = ENABLE_RA; ENABLE_SELECT_RB = ENABLE_RB; SELECT_MUX_B = ENABLE_MUX_B

  // Notes on the sheet:
  //   STAGE 3
  //   STAGE COUNTER
  //   STAGE 4
  //   STAGE 2
  //   STAGE 5
endmodule
