// Logisim project miniCPU.circ as structural Verilog: 6 circuits, main circuit main
module main (
  input  En_Hardcode,
  input  [31:0] Hardcoded_Data_32_bit,
  input  [7:0] Hardcoded_Address_8_bit,
  input  [31:0] Hardcoded_Reg_Val_32_bit,
  input  [2:0] Hardcoded_Reg_Add_3_bit
);

  wire CLEAR_CU, CLEAR_MEMORY, CLEAR_Reg, clock_1_out, control_unit_1_inter, EN_IMMEDIATE, EN_MEM_DATA,
       EN_RM, EN_WRITE, INTERRUPT, MEM_TRIGGER, multiplexer_1_out, not_2_out, or_1_out, or_2_out, or_3_out,
       or_4_out, Reg_TRIGGER, STAGE_1, STAGE_2, STAGE_3, STAGE_4, STAGE_5;
  wire [2:0] multiplexer_4_out, OP_TYPE, RA_ADDRESS, RB_ADDRESS, RY_ADDRESS;
  wire [3:0] OPCODE;
  wire [7:0] bit_extender_3_out, MEM_ADDRESS;
  wire [15:0] instruction_register_1_immdeiate;
  wire [31:0] adder_1_out, alu_1_rz, bit_extender_1_out, IMMEDIATE_VAL, IR_q, MEM_DATA, multiplexer_2_out,
       multiplexer_3_out, multiplexer_5_out, multiplexer_6_out, multiplexer_7_out, PC_VALUE, Ra_q, Rb_q,
       register_file_1_ra_val, register_file_1_rb_val, RM_VALUE, Ry_q, RZ_VALUE;

  assign bit_extender_1_out = {{31{1'b0}}, 1'b1};  // Bit_Extender bit_extender_1
  Adder #(.width(32)) adder_1 (.a(PC_VALUE), .b(bit_extender_1_out), .out(adder_1_out));  // open: cin, cout
  Instruction_Register instruction_register_1 (
    .Instruction(IR_q), .Opcode(OPCODE), .Ri_Stored(RY_ADDRESS), .Rj_Op1(RA_ADDRESS), .Rk_Op2(RB_ADDRESS),
    .Immdeiate(instruction_register_1_immdeiate));
  Register #(.width(32)) IR (.D(MEM_DATA), .en(INTERRUPT), .Q(IR_q), .clk(STAGE_1), .clr(CLEAR_CU));
  Control_Unit control_unit_1 (
    .mem_data(EN_MEM_DATA), .rm(EN_RM), .s1(STAGE_1), .s2(STAGE_2), .imm(EN_IMMEDIATE), .s3(STAGE_3),
    .write(EN_WRITE), .s4(STAGE_4), .optype(OP_TYPE), .s5(STAGE_5), .OPCODE(OPCODE), .clear(CLEAR_CU),
    .inter(control_unit_1_inter));
  Register #(.width(32)) PC (.D(adder_1_out), .en(INTERRUPT), .Q(PC_VALUE), .clk(STAGE_1), .clr(CLEAR_CU));
  assign IMMEDIATE_VAL = {{16{1'b0}}, instruction_register_1_immdeiate};  // Bit_Extender bit_extender_2
  not not_1 (INTERRUPT, control_unit_1_inter);
  Multiplexer #(.enable("false")) multiplexer_1 (
    .in0(STAGE_5), .in1(Reg_TRIGGER), .out(multiplexer_1_out), .sel(En_Hardcode));
  Register #(.width(32)) Ra (.D(register_file_1_ra_val), .Q(Ra_q), .clk(STAGE_2), .clr(CLEAR_Reg));  // open: en
  Multiplexer #(.width(32)) multiplexer_2 (
    .in0(Ry_q), .in1(Hardcoded_Reg_Val_32_bit), .out(multiplexer_2_out), .sel(En_Hardcode));  // open: en
  Register_File register_file_1 (
    .clk_5(multiplexer_1_out), .Ry(multiplexer_4_out), .Rb(RB_ADDRESS), .Ra(RA_ADDRESS),
    .Ry_val(multiplexer_2_out), .Ra_val(register_file_1_ra_val), .Rb_val(register_file_1_rb_val),
    .clear(CLEAR_Reg));
  ALU alu_1 (.op_type(OP_TYPE), .Rb(multiplexer_5_out), .Rz(alu_1_rz), .Ra(Ra_q));
  Register #(.width(32)) Rz (.D(alu_1_rz), .Q(RZ_VALUE), .clk(STAGE_3), .clr(CLEAR_Reg));  // open: en
  Register #(.width(32)) Rb (.D(register_file_1_rb_val), .Q(Rb_q), .clk(STAGE_2), .clr(CLEAR_Reg));  // open: en
  Multiplexer #(.width(32), .enable("false")) multiplexer_3 (
    .in0(RZ_VALUE), .in1(MEM_DATA), .out(multiplexer_3_out), .sel(EN_MEM_DATA));
  Register #(.width(32)) Ry (.D(multiplexer_3_out), .Q(Ry_q), .clk(STAGE_4), .clr(CLEAR_Reg));  // open: en
  Multiplexer #(.width(3), .enable("false")) multiplexer_4 (
    .in0(RY_ADDRESS), .in1(Hardcoded_Reg_Add_3_bit), .out(multiplexer_4_out), .sel(En_Hardcode));
  Multiplexer #(.width(32)) multiplexer_5 (
    .in0(Rb_q), .in1(IMMEDIATE_VAL), .out(multiplexer_5_out), .sel(EN_IMMEDIATE));  // open: en
  Register #(.width(32)) Rm (.D(Rb_q), .en(EN_RM), .Q(RM_VALUE), .clk(STAGE_3), .clr(CLEAR_Reg));
  Button button_1 (.out(CLEAR_CU));
  Clock clock_1 (.out(clock_1_out));
  Multiplexer #(.width(32), .enable("false")) multiplexer_6 (
    .in0(PC_VALUE), .in1(RZ_VALUE), .out(multiplexer_6_out), .sel(or_1_out));
  or or_1 (or_1_out, STAGE_3, STAGE_4);
  Counter counter_1 (
    .main_clk(clock_1_out), .reset_clk(CLEAR_CU), .clk_1(STAGE_1), .clk_2(STAGE_2), .clk_3(STAGE_3),
    .clk_4(STAGE_4), .clk_5(STAGE_5));
  Button button_2 (.out(CLEAR_Reg));
  Button button_3 (.out(CLEAR_MEMORY));
  Bit_Extender #(.in_width(32), .out_width(8)) bit_extender_3 (.in(multiplexer_6_out), .out(bit_extender_3_out));
  Multiplexer #(.width(32), .enable("false")) multiplexer_7 (
    .in0(RM_VALUE), .in1(Hardcoded_Data_32_bit), .out(multiplexer_7_out), .sel(En_Hardcode));
  or or_2 (or_2_out, EN_WRITE, En_Hardcode);
  Multiplexer #(.width(8), .enable("false")) multiplexer_8 (
    .in0(bit_extender_3_out), .in1(Hardcoded_Address_8_bit), .out(MEM_ADDRESS), .sel(En_Hardcode));
  Multiplexer #(.width(32), .enable("false")) multiplexer_9 (
    .in1(multiplexer_7_out), .out(MEM_DATA), .sel(or_2_out));  // open: in0
  or or_3 (or_3_out, STAGE_4, MEM_TRIGGER);
  or or_4 (or_4_out, EN_WRITE, En_Hardcode);
  Clock Memory_Trigger (.out(MEM_TRIGGER));
  Clock Register_Trigger (.out(Reg_TRIGGER));
  not not_2 (not_2_out, or_4_out);
  RAM #(.dataWidth(32)) ram_1 (
    .addr(MEM_ADDRESS), .data(MEM_DATA), .clk(or_3_out), .ld(not_2_out), .clr(CLEAR_MEMORY));  // open: sel

  // Other names for the same wires on the sheet: CLEAR_REG_FILE = CLEAR_Reg; CLEAR_Ry = CLEAR_Reg;
  //   HARDCODED_ADDRESS[7:0] = Hardcoded_Address_8_bit; HARDCODED_DATA[31:0] = Hardcoded_Data_32_bit;
  //   HARDCODED_REG_ADD[2:0] = Hardcoded_Reg_Add_3_bit; HARDCODED_REG_VAL[31:0] = Hardcoded_Reg_Val_32_bit;
  //   READ_MEMORY[31:0] = MEM_DATA; CLEAR_PC = CLEAR_CU; RESET_CLOCK = CLEAR_CU

  // Notes on the sheet:
  //   Opcode   Ry   Ra  Rb  Immediate
  //   1 0 0 0 3
  //   1 1 0 0 4
  //   4 2 1 0 0
  //   3 0 0 2 2
  //   12 0 0 0 0
endmodule

module Register_File (
  input  [31:0] Ry_val,
  input  [2:0] Ry,
  input  clk_5,
  input  [2:0] Rb,
  input  [2:0] Ra,
  input  clear,
  output [31:0] Ra_val,
  output [31:0] Rb_val
);

  wire decoder_1_out0, decoder_1_out1, decoder_1_out2, decoder_1_out3, decoder_1_out4, decoder_1_out5,
       decoder_1_out6, decoder_1_out7;
  wire [31:0] demultiplexer_1_out0, demultiplexer_1_out1, demultiplexer_1_out2, demultiplexer_1_out3,
       demultiplexer_1_out4, demultiplexer_1_out5, demultiplexer_1_out6, demultiplexer_1_out7, register_1_q,
       register_2_q, register_3_q, register_4_q, register_5_q, register_6_q, register_7_q, register_8_q;

  Register #(.width(32)) register_1 (
    .D(demultiplexer_1_out0), .en(decoder_1_out0), .Q(register_1_q), .clk(clk_5), .clr(clear));
  Register #(.width(32)) register_2 (
    .D(demultiplexer_1_out4), .en(decoder_1_out4), .Q(register_2_q), .clk(clk_5), .clr(clear));
  Multiplexer #(.select(3), .width(32)) multiplexer_1 (
    .in0(register_1_q), .in1(register_3_q), .in2(register_5_q), .in3(register_7_q), .in4(register_2_q),
    .in5(register_4_q), .in6(register_6_q), .in7(register_8_q), .out(Ra_val), .sel(Ra));  // open: en
  Register #(.width(32)) register_3 (
    .D(demultiplexer_1_out1), .en(decoder_1_out1), .Q(register_3_q), .clk(clk_5), .clr(clear));
  Register #(.width(32)) register_4 (
    .D(demultiplexer_1_out5), .en(decoder_1_out5), .Q(register_4_q), .clk(clk_5), .clr(clear));
  Demultiplexer #(.select(3), .width(32), .enable("false")) demultiplexer_1 (
    .out0(demultiplexer_1_out0), .out1(demultiplexer_1_out1), .out2(demultiplexer_1_out2),
    .out3(demultiplexer_1_out3), .out4(demultiplexer_1_out4), .out5(demultiplexer_1_out5),
    .out6(demultiplexer_1_out6), .out7(demultiplexer_1_out7), .in(Ry_val), .sel(Ry));
  Register #(.width(32)) register_5 (
    .D(demultiplexer_1_out2), .en(decoder_1_out2), .Q(register_5_q), .clk(clk_5), .clr(clear));
  Register #(.width(32)) register_6 (
    .D(demultiplexer_1_out6), .en(decoder_1_out6), .Q(register_6_q), .clk(clk_5), .clr(clear));
  Register #(.width(32)) register_7 (
    .D(demultiplexer_1_out3), .en(decoder_1_out3), .Q(register_7_q), .clk(clk_5), .clr(clear));
  Register #(.width(32)) register_8 (
    .D(demultiplexer_1_out7), .en(decoder_1_out7), .Q(register_8_q), .clk(clk_5), .clr(clear));
  Multiplexer #(.select(3), .width(32)) multiplexer_2 (
    .in0(register_1_q), .in1(register_3_q), .in2(register_5_q), .in3(register_7_q), .in4(register_2_q),
    .in5(register_4_q), .in6(register_6_q), .in7(register_8_q), .out(Rb_val), .sel(Rb));  // open: en
  Decoder #(.select(3), .enable("false")) decoder_1 (
    .out0(decoder_1_out0), .out1(decoder_1_out1), .out2(decoder_1_out2), .out3(decoder_1_out3),
    .out4(decoder_1_out4), .out5(decoder_1_out5), .out6(decoder_1_out6), .out7(decoder_1_out7), .sel(Ry));
endmodule

module ALU (
  input  [31:0] Ra,
  input  [31:0] Rb,
  input  [2:0] op_type,
  output [31:0] Rz
);

  wire [31:0] adder_1_out, and_1_out, or_1_out, subtractor_1_out;

  Adder #(.width(32)) adder_1 (.a(Rb), .b(Ra), .out(adder_1_out));  // open: cin, cout
  Subtractor #(.width(32)) subtractor_1 (.a(Ra), .b(Rb), .out(subtractor_1_out));  // open: bin, bout
  Multiplexer #(.select(3), .width(32)) multiplexer_1 (
    .in0(Ra), .in1(adder_1_out), .in2(subtractor_1_out), .in3(and_1_out), .in4(or_1_out), .in5(Rb), .out(Rz),
    .sel(op_type));  // open: in6, in7, en
  assign and_1_out = Rb & Ra;  // AND_Gate and_1, 32 bits wide
  assign or_1_out = Ra | Rb;  // OR_Gate or_1, 32 bits wide

  // Notes on the sheet:
  //   0 for Ra bypass
  //   1 for add Ra+Rb
  //   2 for Ra-Rb
  //   3 for Ra & Rb
  //   4 for Ra | Rb
  //   5 for Rb bypass
endmodule

module Control_Unit (
  input  s1,
  input  s2,
  input  s3,
  input  s4,
  input  s5,
  input  clear,
  input  [3:0] OPCODE,
  output mem_data,
  output rm,
  output imm,
  output write,
  output [2:0] optype,
  output inter
);

  wire ADD, ADI, AND, ANI, EN_IMMEDIATE, EN_MEM_DATA, EN_RM, HLT, MOI, MOV, OR, or_2_out, or_3_out, or_4_out,
       or_5_out, ORI, SUB, SUI;
  wire [2:0] ANDOP, BBP, MINUS, OROP, PLUS;

  Decoder #(.select(4)) decoder_1 (
    .out0(MOV), .out1(MOI), .out2(EN_MEM_DATA), .out3(EN_RM), .out4(ADD), .out5(ADI), .out6(SUB), .out7(SUI),
    .out8(AND), .out9(ANI), .out10(OR), .out11(ORI), .out12(HLT), .sel(OPCODE));  // open: out13, out14, out15, en
  or or_1 (EN_IMMEDIATE, MOI, EN_MEM_DATA, EN_RM, ADI, SUI, ANI, ORI);
  or or_2 (or_2_out, EN_MEM_DATA, EN_RM, ADD, ADI);
  or or_3 (or_3_out, SUB, SUI);
  Multiplexer #(.width(3), .enable("false")) multiplexer_1 (.in0(3'b000), .in1(3'b001), .out(PLUS), .sel(or_2_out));
  Multiplexer #(.width(3), .enable("false")) multiplexer_2 (.in0(3'b000), .in1(3'b010), .out(MINUS), .sel(or_3_out));
  or or_4 (or_4_out, OR, ORI);
  Multiplexer #(.width(3), .enable("false")) multiplexer_3 (.in0(3'b000), .in1(3'b011), .out(ANDOP), .sel(or_5_out));
  or or_5 (or_5_out, AND, ANI);
  Multiplexer #(.width(3), .enable("false")) multiplexer_4 (.in0(3'b000), .in1(3'b100), .out(OROP), .sel(or_4_out));
  Multiplexer #(.enable("false")) multiplexer_5 (.in0(EN_MEM_DATA), .in1(1'b0), .out(mem_data), .sel(clear));
  Multiplexer #(.enable("false")) multiplexer_6 (.in0(EN_RM), .in1(1'b0), .out(rm), .sel(clear));
  Multiplexer #(.enable("false")) multiplexer_7 (.in0(EN_IMMEDIATE), .in1(1'b0), .out(imm), .sel(clear));
  Multiplexer #(.enable("false")) multiplexer_8 (.in0(EN_RM), .in1(1'b0), .out(write), .sel(clear));
  Multiplexer #(.enable("false")) multiplexer_9 (.in0(HLT), .in1(1'b0), .out(inter), .sel(clear));
  Multiplexer #(.width(3), .enable("false")) multiplexer_10 (.in0(3'b000), .in1(3'b101), .out(BBP), .sel(MOI));
  assign optype = ANDOP | PLUS | MINUS | BBP | OROP;  // OR_Gate or_6, 3 bits wide

  // Other names for the same wires on the sheet: INTERRUPT = HLT; LOAD = EN_MEM_DATA; OP_TYPE[2:0] = optype;
  //   STAGE_1 = s1; STAGE_2 = s2; STAGE_3 = s3; STAGE_4 = s4; STAGE_5 = s5; EN_WRITE = EN_RM; STORE = EN_RM
endmodule

module Instruction_Register (
  input  [31:0] Instruction,
  output [3:0] Opcode,
  output [2:0] Ri_Stored,
  output [2:0] Rj_Op1,
  output [2:0] Rk_Op2,
  output [15:0] Immdeiate
);


  assign Immdeiate = Instruction[15:0];
  assign Opcode = Instruction[31:28];
  assign Ri_Stored = Instruction[26:24];
  assign Rj_Op1 = Instruction[22:20];
  assign Rk_Op2 = Instruction[18:16];

  // Other names for the same wires on the sheet: Immediate[15:0] = Instruction[15:0]; Ri[2:0] = Instruction[26:24];
  //   Rj[2:0] = Instruction[22:20]; Rk[2:0] = Instruction[18:16]
endmodule

module Counter (
  input  main_clk,
  input  reset_clk,
  output clk_1,
  output clk_2,
  output clk_3,
  output clk_4,
  output clk_5
);

  wire j_k_ff_1_qn, j_k_ff_2_qn, j_k_ff_3_qn, j_k_ff_4_qn, j_k_ff_5_qn;

  J_K_Flip_Flop j_k_ff_1 (
    .J(clk_5), .clk(main_clk), .K(j_k_ff_5_qn), .Q(clk_1), .Qn(j_k_ff_1_qn), .reset(reset_clk));  // open: preset, en
  J_K_Flip_Flop j_k_ff_2 (
    .J(clk_1), .clk(main_clk), .K(j_k_ff_1_qn), .Q(clk_2), .Qn(j_k_ff_2_qn), .reset(reset_clk));  // open: preset, en
  J_K_Flip_Flop j_k_ff_3 (
    .J(clk_2), .clk(main_clk), .K(j_k_ff_2_qn), .Q(clk_3), .Qn(j_k_ff_3_qn), .reset(reset_clk));  // open: preset, en
  J_K_Flip_Flop j_k_ff_4 (
    .J(clk_3), .clk(main_clk), .K(j_k_ff_3_qn), .Q(clk_4), .Qn(j_k_ff_4_qn), .reset(reset_clk));  // open: preset, en
  J_K_Flip_Flop j_k_ff_5 (
    .J(clk_4), .clk(main_clk), .K(j_k_ff_4_qn), .Q(clk_5), .Qn(j_k_ff_5_qn), .preset(reset_clk));  // open: en, reset
endmodule
